# Fritzing sketch Skecth (saved by Fritzing 0.9.3b)
breadboards: 1

parts:
  U1 = 2-Channel 5v Relay Shield [package=relay-2ch5v10a]
  R1 = Rotary Potentiometer (Small) [maximum_resistance=100kΩ package=THT]
  R2 = Photocell (LDR) [package=THT]
  LED1 = LED - 5mm [color="Red (633nm)" package="5 mm [THT]"]
  LED2 = LED - 5mm [color="Red (633nm)" package="5 mm [THT]"]
  PIR1 = PIR sensor
  R3 = Resistor [tolerance=±5% resistance=220 package=THT]
  R4 = Resistor [tolerance=±5% resistance=220 package=THT]  # not connected
  R5 = Resistor [tolerance=±5% resistance=220 package=THT]
  U3 = NodeMCU V3.0
  R6 = Resistor [tolerance=±5% resistance=220 package="0603 [SMD]"]

nets:
  VCC: U1.VCC, U1.K2-On, PIR1.VDD, U3.3V3
  N1: U1.GND, U3.GND#41
  N2: U1.IN2, U3.D2
  N3: U1.K2-In, LED2.cathode
  N4: U1.JD-GND, R2.pin_1
  N5: R1.leg1, R6.Pin_0
  N6: R1.wiper, R5.Pin_1
  N7: R1.leg2, U3.D3
  N8: LED1.cathode, U3.D1
  N9: LED1.anode, R3.Pin_1
  N10: LED2.anode, PIR1.GND, U3.GND#6, U3.GND#13, U3.GND#16, U3.GND#33, R6.Pin_1
  N11: PIR1.SIG, U3.D0
  N12: R3.Pin_0, R5.Pin_0, U3.A0

custom parts:
  2-Channel 5v Relay Shield: 2 Channel 5v Relay Shield w. 2x SPD-06VDC-SD-C
  NodeMCU V3.0: ESP8266 based NodeMCU
